// Digital circuit Circuit.dig as structural Verilog
module Circuit (
  input  in_1,
  input  in_2
);

  wire u_hw_s;

  hw #(.applicationType("GHDL")) u_hw (.A(in_1), .B(in_2), .S(u_hw_s));
  LED led_1 (.in(u_hw_s));
endmodule

/* Code of hw:
library ieee;
use IEEE.std_logic_1164.all;

entity hw is
    port(
        A: in STD_LOGIC;
        B: in STD_LOGIC;
        S: out STD_LOGIC
    );
end hw;

architecture comportamento of hw is
begin
    S <= A and B;
end comportamento;
*/
